// Logisim project lab3.circ as structural Verilog
module OneBitFullAdder (
  input  A,
  input  B,
  input  C_in,
  output S,
  output C_out
);

  wire and_1_out, and_2_out, and_3_out, and_4_out, and_5_out, and_6_out, and_7_out, not_1_out, not_2_out,
       not_3_out;

  not not_1 (not_1_out, A);
  not not_2 (not_2_out, B);
  not not_3 (not_3_out, C_in);
  and and_1 (and_1_out, not_1_out, not_2_out, C_in);
  and and_2 (and_2_out, not_1_out, B, not_3_out);
  and and_3 (and_3_out, A, not_2_out, not_3_out);
  and and_4 (and_4_out, A, B, C_in);
  and and_5 (and_5_out, B, C_in);
  and and_6 (and_6_out, A, C_in);
  and and_7 (and_7_out, A, B);
  or or_1 (S, and_1_out, and_2_out, and_3_out, and_4_out);
  or or_2 (C_out, and_5_out, and_6_out, and_7_out);
endmodule

module ALUControlCircuit (
  input  I30,
  input  I14,
  input  I13,
  input  I12,
  input  I6,
  input  I5,
  input  I4,
  output ALU_Ctrl3,
  output ALU_Ctrl2,
  output ALU_Ctrl1,
  output ALU_Ctrl0,
  output ALU_Src
);

  wire and_2_out, not_1_out, not_2_out, not_3_out, not_4_out, not_5_out;

  not not_1 (not_1_out, I14);
  not not_2 (not_2_out, I13);
  not not_3 (not_3_out, I12);
  not not_4 (not_4_out, I5);
  not not_5 (not_5_out, I4);
  and and_1 (ALU_Ctrl2, I30, not_2_out, I5);
  or or_1 (ALU_Ctrl1, not_2_out, not_5_out);
  and and_2 (and_2_out, I13, not_3_out);
  or or_2 (ALU_Src, not_4_out, not_5_out);
  or or_3 (ALU_Ctrl0, not_1_out, and_2_out);

  assign ALU_Ctrl3 = 1'b0;
endmodule

module OneBitALU (
  input  [3:0] ALU_Ctrl,
  input  A,
  input  B,
  input  C_in,
  output R,
  output C_out
);

  wire and_1_out, multiplexer_1_out, not_1_out, onebitfulladder_1_s, or_1_out, xor_1_out;

  not not_1 (not_1_out, B);
  Multiplexer #(.enable("false")) multiplexer_1 (.in0(B), .in1(not_1_out), .out(multiplexer_1_out), .sel(ALU_Ctrl[2]));
  and and_1 (and_1_out, A, multiplexer_1_out);
  or or_1 (or_1_out, A, multiplexer_1_out);
  xor xor_1 (xor_1_out, A, multiplexer_1_out);
  Multiplexer #(.enable("false"), .select(2)) multiplexer_2 (
    .in0(and_1_out), .in1(or_1_out), .in2(xor_1_out), .in3(onebitfulladder_1_s), .out(R), .sel(ALU_Ctrl[1:0]));
  OneBitFullAdder onebitfulladder_1 (.A(A), .B(multiplexer_1_out), .C_in(C_in), .S(onebitfulladder_1_s), .C_out(C_out));
endmodule

module ALU32 (
  input  [3:0] ALU_Ctrl,
  input  [31:0] A,
  input  [31:0] B,
  output [31:0] R,
  output C_out
);

  wire alu4_1_c_out, alu4_2_c_out, alu4_3_c_out, alu4_4_c_out, alu4_5_c_out, alu4_6_c_out, alu4_7_c_out;

  ALU4 alu4_1 (.ALU_Ctrl(ALU_Ctrl), .A(A[3:0]), .B(B[3:0]), .C_in(ALU_Ctrl[2]), .R(R[3:0]), .C_out(alu4_1_c_out));
  ALU4 alu4_2 (.ALU_Ctrl(ALU_Ctrl), .A(A[7:4]), .B(B[7:4]), .C_in(alu4_1_c_out), .R(R[7:4]), .C_out(alu4_2_c_out));
  ALU4 alu4_3 (.ALU_Ctrl(ALU_Ctrl), .A(A[11:8]), .B(B[11:8]), .C_in(alu4_2_c_out), .R(R[11:8]), .C_out(alu4_3_c_out));
  ALU4 alu4_4 (
    .ALU_Ctrl(ALU_Ctrl), .A(A[15:12]), .B(B[15:12]), .C_in(alu4_3_c_out), .R(R[15:12]), .C_out(alu4_4_c_out));
  ALU4 alu4_5 (
    .ALU_Ctrl(ALU_Ctrl), .A(A[19:16]), .B(B[19:16]), .C_in(alu4_4_c_out), .R(R[19:16]), .C_out(alu4_5_c_out));
  ALU4 alu4_6 (
    .ALU_Ctrl(ALU_Ctrl), .A(A[23:20]), .B(B[23:20]), .C_in(alu4_5_c_out), .R(R[23:20]), .C_out(alu4_6_c_out));
  ALU4 alu4_7 (
    .ALU_Ctrl(ALU_Ctrl), .A(A[27:24]), .B(B[27:24]), .C_in(alu4_6_c_out), .R(R[27:24]), .C_out(alu4_7_c_out));
  ALU4 alu4_8 (.ALU_Ctrl(ALU_Ctrl), .A(A[31:28]), .B(B[31:28]), .C_in(alu4_7_c_out), .R(R[31:28]), .C_out(C_out));
endmodule

module ALU4 (
  input  [3:0] ALU_Ctrl,
  input  [3:0] A,
  input  [3:0] B,
  input  C_in,
  output [3:0] R,
  output C_out
);

  wire onebitalu_1_c_out, onebitalu_2_c_out, onebitalu_3_c_out;

  OneBitALU onebitalu_1 (.ALU_Ctrl(ALU_Ctrl), .A(A[0]), .B(B[0]), .C_in(C_in), .R(R[0]), .C_out(onebitalu_1_c_out));
  OneBitALU onebitalu_2 (
    .ALU_Ctrl(ALU_Ctrl), .A(A[1]), .B(B[1]), .C_in(onebitalu_1_c_out), .R(R[1]), .C_out(onebitalu_2_c_out));
  OneBitALU onebitalu_3 (
    .ALU_Ctrl(ALU_Ctrl), .A(A[2]), .B(B[2]), .C_in(onebitalu_2_c_out), .R(R[2]), .C_out(onebitalu_3_c_out));
  OneBitALU onebitalu_4 (.ALU_Ctrl(ALU_Ctrl), .A(A[3]), .B(B[3]), .C_in(onebitalu_3_c_out), .R(R[3]), .C_out(C_out));
endmodule

module Datapath (
  input  [31:0] Instruction
);

  wire alucontrolcircuit_1_alu_src;
  wire [3:0] alucontrolcircuit_1_alu_ctrl0;
  wire [31:0] bit_extender_1_out, multiplexer_1_out, undriven_2, undriven_3;
  wire [31:4] undriven;

  Clock clock_1 ();  // open: out
  assign bit_extender_1_out = {{20{undriven[31]}}, undriven[31:20]};  // Bit_Extender bit_extender_1
  Multiplexer #(.enable("false"), .width(32)) multiplexer_1 (
    .in0(undriven_3), .in1(bit_extender_1_out), .out(multiplexer_1_out), .sel(alucontrolcircuit_1_alu_src));
  ALUControlCircuit alucontrolcircuit_1 (
    .I30(undriven[30]), .I14(undriven[14]), .I13(undriven[13]), .I12(undriven[12]), .I6(undriven[6]),
    .I5(undriven[5]), .I4(undriven[4]), .ALU_Ctrl3(alucontrolcircuit_1_alu_ctrl0[3]),
    .ALU_Ctrl2(alucontrolcircuit_1_alu_ctrl0[2]), .ALU_Ctrl1(alucontrolcircuit_1_alu_ctrl0[1]),
    .ALU_Ctrl0(alucontrolcircuit_1_alu_ctrl0[0]), .ALU_Src(alucontrolcircuit_1_alu_src));
  ALU32 alu32_1 (.ALU_Ctrl(alucontrolcircuit_1_alu_ctrl0), .A(undriven_2), .B(multiplexer_1_out));  // open: R, C_out
endmodule

module register_file (
  input  [4:0] RReg2,
  input  Clock_in,
  input  [31:0] WData,
  input  Write,
  input  [4:0] Wreg,
  input  [4:0] RReg1,
  output [31:0] RData1,
  output [31:0] RData2
);

  Demultiplexer #(.enable("false"), .select(5), .width(32)) demultiplexer_1 ();  // open: out0, out1, out2, out3, out4, out5, out6, out7, out8, out9, out10, out11, out12, out13, out14, out15, out16, out17, out18, out19, out20, out21, out22, out23, out24, out25, out26, out27, out28, out29, out30, out31, in, sel
  Register #(.width(32)) register_1 (.D(WData));  // open: en, clk, Q, clr
  Register #(.width(32)) register_2 (.D(WData));  // open: en, clk, Q, clr
  Register #(.width(32)) register_3 (.D(WData));  // open: en, clk, Q, clr
  Register #(.width(32)) register_4 (.D(WData));  // open: en, clk, Q, clr
  Register #(.width(32)) register_5 (.D(WData));  // open: en, clk, Q, clr
  Register #(.width(32)) register_6 (.D(WData));  // open: en, clk, Q, clr
  Register #(.width(32)) register_7 (.D(WData));  // open: en, clk, Q, clr
  Register #(.width(32)) register_8 (.D(WData));  // open: en, clk, Q, clr
  Register #(.width(32)) register_9 (.D(WData));  // open: en, clk, Q, clr
  Register #(.width(32)) register_10 (.D(WData));  // open: en, clk, Q, clr
  Register #(.width(32)) register_11 (.D(WData));  // open: en, clk, Q, clr
  Register #(.width(32)) register_12 (.D(WData));  // open: en, clk, Q, clr
  Register #(.width(32)) register_13 (.D(WData));  // open: en, clk, Q, clr
  Register #(.width(32)) register_14 (.D(WData));  // open: en, clk, Q, clr
  Register #(.width(32)) register_15 (.D(WData));  // open: en, clk, Q, clr
  Register #(.width(32)) register_16 (.D(WData));  // open: en, clk, Q, clr
  Register #(.width(32)) register_17 (.D(WData));  // open: en, clk, Q, clr
  Register #(.width(32)) register_18 (.D(WData));  // open: en, clk, Q, clr
  Register #(.width(32)) register_19 (.D(WData));  // open: en, clk, Q, clr
  Register #(.width(32)) register_20 (.D(WData));  // open: en, clk, Q, clr
  Register #(.width(32)) register_21 (.D(WData));  // open: en, clk, Q, clr
  Register #(.width(32)) register_22 (.D(WData));  // open: en, clk, Q, clr
  Register #(.width(32)) register_23 (.D(WData));  // open: en, clk, Q, clr
  Register #(.width(32)) register_24 (.D(WData));  // open: en, clk, Q, clr
  Register #(.width(32)) register_25 (.D(WData));  // open: en, clk, Q, clr
  Register #(.width(32)) register_26 (.D(WData));  // open: en, clk, Q, clr
  Register #(.width(32)) register_27 (.D(WData));  // open: en, clk, Q, clr
  Register #(.width(32)) register_28 (.D(WData));  // open: en, clk, Q, clr
  Register #(.width(32)) register_29 (.D(WData));  // open: en, clk, Q, clr
  Register #(.width(32)) register_30 (.D(WData));  // open: en, clk, Q, clr
  Register #(.width(32)) register_31 (.D(WData));  // open: en, clk, Q, clr
  Register #(.width(32)) register_32 (.D(WData));  // open: en, clk, Q, clr
  Multiplexer #(.enable("false"), .select(5), .width(32)) multiplexer_1 (
    .out(RData1), .sel(RReg2));  // open: in0, in1, in2, in3, in4, in5, in6, in7, in8, in9, in10, in11, in12, in13, in14, in15, in16, in17, in18, in19, in20, in21, in22, in23, in24, in25, in26, in27, in28, in29, in30, in31
  Multiplexer #(.enable("false"), .select(5), .width(32)) multiplexer_2 (
    .out(RData2), .sel(RReg1));  // open: in0, in1, in2, in3, in4, in5, in6, in7, in8, in9, in10, in11, in12, in13, in14, in15, in16, in17, in18, in19, in20, in21, in22, in23, in24, in25, in26, in27, in28, in29, in30, in31
endmodule

module BarrelShifter (
);

  Shifter #(.shift("lr"), .width(32)) shifter_1 ();  // open: in, dist, out
  Shifter #(.width(32)) shifter_2 ();  // open: in, dist, out
  Shifter #(.shift("lr"), .width(32)) shifter_3 ();  // open: in, dist, out
endmodule
